// Logisim project ALU实验step.circ as structural Verilog: 1 circuit, main circuit main
module main (
  input  [31:0] X,
  input  [31:0] Y,
  input  [1:0] Aluop,
  input  [4:0] ShiftNum,
  output [31:0] R,
  output OF,
  output [31:0] R2,
  output equal
);

  wire [31:0] adder_1_out, multiplier_1_out, shifter_1_out;

  Adder #(.width(32)) adder_1 (.a(X), .b(Y), .out(adder_1_out), .cout(OF));  // open: cin
  Multiplier #(.width(32)) multiplier_1 (.a(X), .b(Y), .out(multiplier_1_out), .cout(R2));  // open: cin
  Comparator #(.width(32), .mode("twosComplement")) comparator_1 (.a(X), .b(Y), .eq(equal));  // open: gt, lt
  Shifter #(.width(32), .shift("ar")) shifter_1 (.in(X), .\dist (ShiftNum), .out(shifter_1_out));
  Multiplexer #(.select(2), .width(32), .disabled("Z"), .enable("false")) multiplexer_1 (
    .in0(adder_1_out), .in1(multiplier_1_out), .in3(shifter_1_out), .out(R), .sel(Aluop));  // open: in2
endmodule
