// Logisim project _4位可控加减法 - 副本.circ as structural Verilog: 1 circuit, main circuit main
module main (
  input  Sub,
  input  X3,
  input  X2,
  input  X1,
  input  X0,
  input  Y3,
  input  Y2,
  input  Y1,
  input  Y0,
  output overflow,
  output S3,
  output S2,
  output S1,
  output S0,
  output Cout
);

  wire xor_2_out, \一位全加器fa封装1_1_p5 , \一位全加器fa封装1_2_p4 , \一位全加器fa封装1_2_p5 , \一位全加器fa封装1_3_p4 ,
       \一位全加器fa封装1_3_p5 , \一位全加器fa封装1_4_p4 ;

  xor xor_1 (overflow, Cout, \一位全加器fa封装1_1_p5 );
  xor xor_2 (xor_2_out, Y3, Sub);
  // 一位全加器FA封装1 一位全加器fa封装1_1: pin names not known; wires that end beside it: Cout, X3, S3, xor_2_out, \一位全加器fa封装1_1_p5 
  // 一位全加器FA封装1 一位全加器fa封装1_2: pin names not known; wires that end beside it: \一位全加器fa封装1_1_p5 , X2, S2, \一位全加器fa封装1_2_p4 , \一位全加器fa封装1_2_p5 
  xor xor_3 (\一位全加器fa封装1_2_p4 , Y2, Sub);
  // 一位全加器FA封装1 一位全加器fa封装1_3: pin names not known; wires that end beside it: \一位全加器fa封装1_2_p5 , X1, S1, \一位全加器fa封装1_3_p4 , \一位全加器fa封装1_3_p5 
  xor xor_4 (\一位全加器fa封装1_3_p4 , Y1, Sub);
  // 一位全加器FA封装1 一位全加器fa封装1_4: pin names not known; wires that end beside it: \一位全加器fa封装1_3_p5 , X0, S0, \一位全加器fa封装1_4_p4 , Sub
  xor xor_5 (\一位全加器fa封装1_4_p4 , Y0, Sub);
endmodule
