// Logisim project _8位可控加减法.circ as structural Verilog: 1 circuit, main circuit main
module main (
  input  Sub,
  input  X7,
  input  X6,
  input  X5,
  input  X4,
  input  X3,
  input  X2,
  input  X1,
  input  X0,
  input  Y7,
  input  Y6,
  input  Y5,
  input  Y4,
  input  Y3,
  input  Y2,
  input  Y1,
  input  Y0,
  output overflow,
  output S7,
  output S6,
  output S5,
  output S4,
  output S3,
  output S2,
  output S1,
  output S0,
  output C8
);

  wire xor_6_out, \一位全加器fa封装1_1_p4 , \一位全加器fa封装1_1_p5 , \一位全加器fa封装1_2_p4 , \一位全加器fa封装1_2_p5 ,
       \一位全加器fa封装1_3_p3 , \一位全加器fa封装1_3_p4 , \一位全加器fa封装1_4_p3 , \一位全加器fa封装1_4_p4 , \一位全加器fa封装1_5_p5 ,
       \一位全加器fa封装1_6_p4 , \一位全加器fa封装1_6_p5 , \一位全加器fa封装1_7_p4 , \一位全加器fa封装1_7_p5 , \一位全加器fa封装1_8_p4 ;

  xor xor_1 (overflow, C8, \一位全加器fa封装1_1_p5 );
  // 一位全加器FA封装1 一位全加器fa封装1_1: pin names not known; wires that end beside it: C8, X7, S7, \一位全加器fa封装1_1_p4 , \一位全加器fa封装1_1_p5 
  xor xor_2 (\一位全加器fa封装1_1_p4 , Y7, Sub);
  // 一位全加器FA封装1 一位全加器fa封装1_2: pin names not known; wires that end beside it: \一位全加器fa封装1_1_p5 , X6, S6, \一位全加器fa封装1_2_p4 , \一位全加器fa封装1_2_p5 , \一位全加器fa封装1_2_p5 
  xor xor_3 (\一位全加器fa封装1_2_p4 , Y6, Sub);
  // 一位全加器FA封装1 一位全加器fa封装1_3: pin names not known; wires that end beside it: X5, S5, \一位全加器fa封装1_3_p3 , \一位全加器fa封装1_3_p4 , \一位全加器fa封装1_3_p4 
  xor xor_4 (\一位全加器fa封装1_3_p3 , Y5, Sub);
  // 一位全加器FA封装1 一位全加器fa封装1_4: pin names not known; wires that end beside it: X4, S4, \一位全加器fa封装1_4_p3 , \一位全加器fa封装1_4_p4 
  xor xor_5 (\一位全加器fa封装1_4_p3 , Y4, Sub);
  xor xor_6 (xor_6_out, Y3, Sub);
  // 一位全加器FA封装1 一位全加器fa封装1_5: pin names not known; wires that end beside it: \一位全加器fa封装1_4_p4 , X3, S3, xor_6_out, \一位全加器fa封装1_5_p5 
  // 一位全加器FA封装1 一位全加器fa封装1_6: pin names not known; wires that end beside it: \一位全加器fa封装1_5_p5 , X2, S2, \一位全加器fa封装1_6_p4 , \一位全加器fa封装1_6_p5 
  xor xor_7 (\一位全加器fa封装1_6_p4 , Y2, Sub);
  // 一位全加器FA封装1 一位全加器fa封装1_7: pin names not known; wires that end beside it: \一位全加器fa封装1_6_p5 , X1, S1, \一位全加器fa封装1_7_p4 , \一位全加器fa封装1_7_p5 
  xor xor_8 (\一位全加器fa封装1_7_p4 , Y1, Sub);
  // 一位全加器FA封装1 一位全加器fa封装1_8: pin names not known; wires that end beside it: \一位全加器fa封装1_7_p5 , X0, S0, \一位全加器fa封装1_8_p4 , Sub
  xor xor_9 (\一位全加器fa封装1_8_p4 , Y0, Sub);
endmodule
