// Logisim project 存储系统step2.circ as structural Verilog: 2 circuits, main circuit ◇寄存器组
module \熟悉寄存器的使用  (
  input  [31:0] in_1,
  input  in_2,
  input  in_3,
  output [31:0] out_4
);

  Register #(.width(32), .trigger("rising"), .Select("low")) register_1 (
    .D(in_1), .en(in_2), .Q(out_4), .clk(in_3));  // open: clr

  // Notes on the sheet:
  //   熟悉寄存器的使用：使能端为1且来一个上升沿，两个条件同时满足寄存器才会被写入
endmodule

module \寄存器组  (
  input  [1:0] R1_num,
  input  [1:0] R2_num,
  input  [3:0] Din,
  input  [1:0] Write_Reg_num,
  input  Write_Enable,
  input  Clock,
  output [3:0] Reg1Out,
  output [3:0] Reg2Out
);

  wire and_1_out, and_2_out, and_3_out, and_4_out, w0, w1, w2, w3;
  wire [3:0] reg0, reg1, reg2, reg3;

  Register #(.width(4), .trigger("rising"), .Select("low")) register_1 (
    .D(4'b0000), .en(and_1_out), .Q(reg0), .clk(Clock));  // open: clr
  and and_1 (and_1_out, Write_Enable, w0);
  Register #(.width(4), .trigger("rising"), .Select("low")) register_2 (
    .D(Din), .en(and_2_out), .Q(reg1), .clk(Clock));  // open: clr
  and and_2 (and_2_out, Write_Enable, w1);
  Register #(.width(4), .trigger("rising"), .Select("low")) register_3 (
    .D(Din), .en(and_3_out), .Q(reg2), .clk(Clock));  // open: clr
  and and_3 (and_3_out, Write_Enable, w2);
  Multiplexer #(.select(2), .width(4), .disabled("Z"), .enable("false")) multiplexer_1 (
    .in0(reg0), .in1(reg1), .in2(reg2), .in3(reg3), .out(Reg1Out), .sel(R1_num));
  Register #(.width(4), .trigger("rising"), .Select("low")) register_4 (
    .D(Din), .en(and_4_out), .Q(reg3), .clk(Clock));  // open: clr
  and and_4 (and_4_out, Write_Enable, w3);
  Decoder #(.select(2), .tristate("false"), .disabled("Z"), .enable("false")) decoder_1 (
    .out0(w0), .out1(w1), .out2(w2), .out3(w3), .sel(Write_Reg_num));
  Multiplexer #(.select(2), .width(4), .disabled("Z"), .enable("false")) multiplexer_2 (
    .in0(reg0), .in1(reg1), .in2(reg2), .in3(reg3), .out(Reg2Out), .sel(R2_num));

  // Other names for the same wires on the sheet: CLK = Clock; RD1[3:0] = Reg1Out; RD2[3:0] = Reg2Out;
  //   W_num[1:0] = Write_Reg_num; WE = Write_Enable

  // Notes on the sheet:
  //   输入引脚
  //   注意：自行复制粘贴所需要的隧道
  //   输出引脚
endmodule
