// Logisim project 2t3.2未完成.circ as structural Verilog: 1 circuit, main circuit main
module main (
  input  D,
  input  C,
  input  B,
  input  A,
  output F
);

  wire n7485_1_pin1, n7485_1_pin3, n7485_1_pin6, nand_1_out, nor_1_out, not_1_out;

  _7485 #(.VccGndPorts("false"), .ShowInternalStructure("true")) u_7485_1 (
    .pin1(n7485_1_pin1), .pin2(n7485_1_pin1), .pin3(n7485_1_pin3), .pin4(n7485_1_pin1), .pin6(n7485_1_pin6),
    .pin15(n7485_1_pin1), .pin14(n7485_1_pin1), .pin13(n7485_1_pin1), .pin12(A), .pin11(C), .pin10(B),
    .pin9(D));  // open: pin5, pin7
  not not_1 (not_1_out, D);
  nand nand_1 (nand_1_out, not_1_out, C);
  nor nor_1 (nor_1_out, B, A);
  or or_1 (F, nor_1_out, n7485_1_pin6, nand_1_out);
  // also tied to GND on the sheet: n7485_1_pin1
  // also tied to VCC on the sheet: n7485_1_pin3
endmodule
