// Logisim project 3t1.circ as structural Verilog: 1 circuit, main circuit main
module main (
  input  R,
  input  S,
  output Q,
  output nQ
);

  nor nor_1 (Q, R, nQ);
  nor nor_2 (nQ, Q, S);
  LED #(.active("true")) led_1 (.in(Q));
endmodule
