// Logisim project 3t2.circ as structural Verilog: 1 circuit, main circuit main
module main (
  input  D,
  input  CP,
  output Q,
  output nQ
);

  wire nand_1_out, nand_2_out;

  nand nand_1 (nand_1_out, D, CP);
  nand nand_2 (nand_2_out, nand_1_out, CP);
  nand nand_3 (Q, nand_1_out, nQ);
  nand nand_4 (nQ, Q, nand_2_out);
endmodule
