// Logisim project 3t3未完.circ as structural Verilog: 1 circuit, main circuit main
module main (
  input  nSd,
  input  nRd,
  input  CP,
  input  D,
  output Q,
  output nQ
);

  wire G3_out, G4_out, G5_out, G6_out, undriven;

  nand G5 (G5_out, nSd, G6_out, undriven);
  nand G3 (G3_out, G5_out, nRd);
  nand G4 (G4_out, undriven, CP, G6_out);
  nand G6 (G6_out, G4_out, nRd, D);
  nand G1 (Q, nSd, G3_out, nQ);
  nand G2 (nQ, Q, G4_out, nRd);
endmodule
