// Logisim project 4位二进制超前加法.circ as structural Verilog: 1 circuit, main circuit main
module main (
  input  A4,
  input  B4,
  input  A3,
  input  B3,
  input  B2,
  input  C0_1,
  input  A2,
  input  A1,
  input  B1,
  output S3,
  output S4,
  output C4,
  output S1,
  output S2
);

  _74283 #(.VccGndPorts("false"), .ShowInternalStructure("true")) u_74283_1 (
    .pin1(S2), .pin2(B2), .pin3(A2), .pin4(S1), .pin5(A1), .pin6(B1), .pin7(C0_1), .pin15(B3), .pin14(A3),
    .pin13(S3), .pin12(A4), .pin11(B4), .pin10(S4), .pin9(C4));
endmodule
