// Logisim project 7段数码管译码器的使用.circ as structural Verilog: 1 circuit, main circuit main
module main (
  input  [3:0] in_1
);

  wire displaydecoder_1_p6, displaydecoder_1_p7, displaydecoder_1_p8, displaydecoder_1_p9,
       displaydecoder_1_p10, displaydecoder_1_p11, displaydecoder_1_p12;

  // DisplayDecoder #(.multibit("true")) displaydecoder_1: pin names not known; wires that end beside it: in_1, 1'b1, 1'b1, 1'b1, 1'b1, displaydecoder_1_p6, displaydecoder_1_p7, displaydecoder_1_p8, displaydecoder_1_p9, displaydecoder_1_p10, displaydecoder_1_p11, displaydecoder_1_p12
  _7_Segment_Display #(.active("true")) u_7_segment_display_1 (
    .g(displaydecoder_1_p12), .f(displaydecoder_1_p11), .a(displaydecoder_1_p6), .b(displaydecoder_1_p7),
    .e(displaydecoder_1_p10), .d(displaydecoder_1_p9), .c(displaydecoder_1_p8), .dp(1'b0));
endmodule
