// Logisim project 全加器.circ as structural Verilog: 1 circuit, main circuit main
module main (
  input  Bi,
  input  Ci_1,
  input  Ai,
  output Si,
  output Ci
);

  wire and_1_out, and_2_out, nor_1_out, xor_1_out;

  xor xor_1 (xor_1_out, Bi, Ci_1);
  xor xor_2 (Si, xor_1_out, Ai);
  and and_1 (and_1_out, xor_1_out, Ai);
  and and_2 (and_2_out, Ci_1, Bi);
  not not_1 (Ci, nor_1_out);
  nor nor_1 (nor_1_out, and_1_out, and_2_out);
endmodule
