// Logisim project 分线器的使用.circ as structural Verilog: 1 circuit, main circuit main
module main (
  input  [2:0] in_1,
  input  in_2,
  input  in_3,
  input  in_4,
  input  [2:0] in_5
);

  wire [2:0] and_1_out, and_2_out, undriven, undriven_2;

  assign and_1_out = undriven & in_1;  // AND_Gate and_1, 3 bits wide
  assign and_2_out = undriven_2 & in_5;  // AND_Gate and_2, 3 bits wide
  // RGBLed #(.multibit("false")) rgbled_1: pin names not known; wires that end beside it: and_1_out[0], and_1_out[1], and_1_out[2]
  // RGBLed #(.multibit("false")) rgbled_2: pin names not known; wires that end beside it: and_2_out[0], and_2_out[1], and_2_out[2]
endmodule
