// Logisim project 半加器.circ as structural Verilog: 1 circuit, main circuit main
module main (
  input  Ai,
  input  Bi,
  output Si,
  output Ci
);

  xor xor_1 (Si, Ai, Bi);
  and and_1 (Ci, Bi, Ai);
endmodule
