// Logisim project 四位串行进位加法器.circ as structural Verilog: 1 circuit, main circuit main
module main (
  input  B3,
  input  A3,
  input  B2,
  input  A0,
  input  A1,
  input  B0,
  input  A2,
  input  B1,
  output S3,
  output S2,
  output S1,
  output S0,
  output C3
);

  wire main_2_ci, main_3_ci, main_4_ci;

  \全加器_main  main_1 (.Bi(B3), .Ci_1(main_2_ci), .Ai(A3), .Si(S3), .Ci(C3));
  \全加器_main  main_2 (.Bi(B2), .Ci_1(main_3_ci), .Ai(A2), .Si(S2), .Ci(main_2_ci));
  \全加器_main  main_3 (.Bi(B1), .Ci_1(main_4_ci), .Ai(A1), .Si(S1), .Ci(main_3_ci));
  \全加器_main  main_4 (.Bi(B0), .Ci_1(1'b0), .Ai(A0), .Si(S0), .Ci(main_4_ci));
endmodule
