// Logisim project 2：1mux.circ as structural Verilog: 1 circuit, main circuit main
module main (
  input  D0,
  input  D1,
  input  A,
  output Z
);

  wire and_1_out, and_2_out, not_1_out;

  and and_1 (and_1_out, D0, not_1_out);
  not not_1 (not_1_out, A);
  and and_2 (and_2_out, D1, A);
  or or_1 (Z, and_1_out, and_2_out);
endmodule
