// Logisim project 4：1mux.circ as structural Verilog: 1 circuit, main circuit main
module main (
  input  in_1,
  input  in_2,
  input  in_3,
  input  in_4,
  input  in_5,
  input  in_6,
  output out_7
);

  wire main_1_z, main_2_z;

  _2_1mux_main main_1 (.D0(in_1), .D1(in_2), .A(in_5), .Z(main_1_z));
  _2_1mux_main main_2 (.D0(in_3), .D1(in_4), .A(in_5), .Z(main_2_z));
  _2_1mux_main main_3 (.D0(main_1_z), .D1(main_2_z), .A(in_6), .Z(out_7));
endmodule
