// Logisim project 8：1mux.circ as structural Verilog: 1 circuit, main circuit main
module main (
  input  a3,
  input  a2,
  input  a1,
  input  a0,
  input  a7,
  input  a6,
  input  a5,
  input  sel2,
  input  sel1,
  input  sel0,
  input  a4,
  output out
);

  wire main_1_out_7, main_2_out_7;

  _4_1mux_main main_1 (.in_1(a3), .in_2(a2), .in_3(a1), .in_4(a0), .in_5(sel1), .in_6(sel0), .out_7(main_1_out_7));
  _4_1mux_main main_2 (.in_1(a7), .in_2(a6), .in_3(a5), .in_4(a4), .in_5(sel1), .in_6(sel0), .out_7(main_2_out_7));
  _2_1mux_main main_3 (.D0(main_1_out_7), .D1(main_2_out_7), .A(sel2), .Z(out));
endmodule
