// Logisim project 选用隧道和探针的全加器.circ as structural Verilog: 1 circuit, main circuit main
module main (
  input  Ai,
  input  Bi,
  input  Ci_1,
  output Si,
  output Ci
);

  wire and_1_out, and_2_out, undriven, xor_1_out;

  xor xor_1 (xor_1_out, Bi, undriven);
  // Probe on xor_1_out
  and and_1 (and_1_out, xor_1_out, Ci_1);
  and and_2 (and_2_out, Bi, Ai);
  xor xor_2 (Si, xor_1_out, Ci_1);
  or or_1 (Ci, and_1_out, and_2_out);

  // Notes on the sheet:
  //   探针
endmodule
